# Fritzing sketch alexa-standing-desk-circuit-design (saved by Fritzing 1.0.0d)
breadboards: 1

parts:
  U1 = Optocoupler [package=THT]
  U2 = Optocoupler [package=THT]
  R1 = Resistor [tolerance=±5% resistance=220 package="0402 [SMD]"]
  R2 = Resistor [tolerance=±5% resistance=220 package="0402 [SMD]"]
  A1 = Raspberry Pi Pico W
  S1 = Pushbutton [package="[THT]"]
  S2 = Pushbutton [package="[THT]"]

nets:
  N1: U1.Pin_1, R1.Pin_1
  N2: U1.Pin_2, U2.Pin_2, A1.pin_3, A1.pin_18, A1.pin_33
  N3: U1.Pin_4, S1.Pin_2
  N4: U1.Pin_5, S1.Pin_4
  N5: U2.Pin_1, R2.Pin_1
  N6: U2.Pin_4, S2.Pin_2
  N7: U2.Pin_5, S2.Pin_4
  N8: R1.Pin_0, A1.pin_19
  N9: R2.Pin_0, A1.pin_12

custom parts:
  Raspberry Pi Pico W: Raspberry Pi Pico W. Based around the RP2040 microcontroller the Pico W is a low cost microcontroller device bringing Raspberry Pi quality, cost, and easy of use to the microcontroller space. The areas marked KEEPOUT in pcb silkscreen should not have traces running through them to avoid shorts on a soldered in module!
